// Logisim project test.circ as structural Verilog: 5 circuits, main circuit main
module main (
  input  in_1,
  input  in_2,
  input  in_3,
  input  in_4,
  output out_5,
  output out_6,
  output out_7,
  output out_8,
  output out_9,
  output out_10,
  output out_11
);

  wire n2x_1_out_5, n2x_1_out_6, n2x_1_out_7, n2x_1_out_8, n2x_1_out_9, n8x_1_out_5, n8x_1_out_6,
       n8x_1_out_7, n8x_1_out_8, n8x_1_out_9, n8x_1_out_10, n8x_1_out_11;

  _2x u_2x_1 (
    .in_1(in_1), .in_2(in_2), .in_3(in_3), .in_4(in_4), .out_5(n2x_1_out_5), .out_6(n2x_1_out_6),
    .out_7(n2x_1_out_7), .out_8(n2x_1_out_8), .out_9(n2x_1_out_9));
  _8x u_8x_1 (
    .in_1(in_1), .in_2(in_2), .in_3(in_3), .in_4(in_4), .out_5(n8x_1_out_5), .out_6(n8x_1_out_6),
    .out_7(n8x_1_out_7), .out_8(n8x_1_out_8), .out_9(n8x_1_out_9), .out_10(n8x_1_out_10),
    .out_11(n8x_1_out_11));
  add2x8x add2x8x_1 (
    .in_1(n2x_1_out_5), .in_2(n2x_1_out_6), .in_3(n2x_1_out_7), .in_4(n2x_1_out_8), .in_5(n2x_1_out_9),
    .in_6(n8x_1_out_5), .in_7(n8x_1_out_6), .in_8(n8x_1_out_7), .in_9(n8x_1_out_8), .in_10(n8x_1_out_9),
    .in_11(n8x_1_out_10), .in_12(n8x_1_out_11), .out_14(out_5), .out_15(out_6), .out_16(out_7),
    .out_17(out_8), .out_18(out_9), .out_19(out_10), .out_20(out_11));  // open: out_13
endmodule

module _2x (
  input  in_1,
  input  in_2,
  input  in_3,
  input  in_4,
  output out_5,
  output out_6,
  output out_7,
  output out_8,
  output out_9
);


  assign out_5 = in_1;
  assign out_6 = in_2;
  assign out_7 = in_3;
  assign out_8 = in_4;
  assign out_9 = 1'b0;
endmodule

module _8x (
  input  in_1,
  input  in_2,
  input  in_3,
  input  in_4,
  output out_5,
  output out_6,
  output out_7,
  output out_8,
  output out_9,
  output out_10,
  output out_11
);


  assign out_5 = in_1;
  assign out_6 = in_2;
  assign out_7 = in_3;
  assign out_8 = in_4;
  assign out_9 = 1'b0;
  assign out_10 = 1'b0;
  assign out_11 = 1'b0;
endmodule

module add2x8x (
  input  in_1,
  input  in_2,
  input  in_3,
  input  in_4,
  input  in_5,
  input  in_6,
  input  in_7,
  input  in_8,
  input  in_9,
  input  in_10,
  input  in_11,
  input  in_12,
  output out_13,
  output out_14,
  output out_15,
  output out_16,
  output out_17,
  output out_18,
  output out_19,
  output out_20
);

  wire fulladder_2_menteut, fulladder_3_menteut, fulladder_4_menteut, fulladder_5_menteut,
       fulladder_6_menteut, fulladder_7_menteut;

  FULLADDER fulladder_1 (.A(1'b0), .B(in_6), .MENTEIN(fulladder_2_menteut), .out_4(out_14), .MENTEUT(out_13));
  FULLADDER fulladder_2 (
    .A(1'b0), .B(in_7), .MENTEIN(fulladder_3_menteut), .out_4(out_15), .MENTEUT(fulladder_2_menteut));
  FULLADDER fulladder_3 (
    .A(in_1), .B(in_8), .MENTEIN(fulladder_4_menteut), .out_4(out_16), .MENTEUT(fulladder_3_menteut));
  FULLADDER fulladder_4 (
    .A(in_2), .B(in_9), .MENTEIN(fulladder_5_menteut), .out_4(out_17), .MENTEUT(fulladder_4_menteut));
  FULLADDER fulladder_5 (
    .A(in_3), .B(in_10), .MENTEIN(fulladder_6_menteut), .out_4(out_18), .MENTEUT(fulladder_5_menteut));
  FULLADDER fulladder_6 (
    .A(in_4), .B(in_11), .MENTEIN(fulladder_7_menteut), .out_4(out_19), .MENTEUT(fulladder_6_menteut));
  FULLADDER fulladder_7 (.A(in_5), .B(in_12), .MENTEIN(1'b0), .out_4(out_20), .MENTEUT(fulladder_7_menteut));
endmodule

module FULLADDER (
  input  A,
  input  B,
  input  MENTEIN,
  output out_4,
  output MENTEUT
);

  wire and_1_out, and_2_out, xor_1_out;

  ExactlyOne xor_1 (.out(xor_1_out), .in0(A), .in1(B), .in4(MENTEIN));
  and and_1 (and_1_out, B, A);
  and and_2 (and_2_out, xor_1_out, MENTEIN);
  xor xor_2 (out_4, xor_1_out, MENTEIN);
  or or_1 (MENTEUT, and_1_out, and_2_out);
endmodule
